# Fritzing sketch envinfo_client_rpi (saved by Fritzing 0.9.3b)
breadboards: 1

parts:
  IC1 = MCP3008 8-channel 10-bit ADC [part_number=MCP3008]
  Raspberry_Pi_1 = Raspberry Pi 3 [part_number=RPI-3-V1.2]
  Part1 = Triple Axis Accelerometer Breakout - ADXL335
  R1 = Photocell (LDR) [package=THT]
  R2 = Resistor [tolerance=±5% resistance=220 package=THT]
  T1 = LM35 Temperature Sensor [package="TO92 [THT]"]
  D1 = SOLAR-IXYS [package=solarbit-12x1]
  R3 = Resistor [tolerance=±5% resistance=1k package=THT]
  R4 = Resistor [tolerance=±5% resistance=1k package=THT]

nets:
  N1: IC1.no_name_yet#1, Part1.XOUT
  N2: IC1.no_name_yet#2, Part1.YOUT
  N3: IC1.no_name_yet#3, Part1.ZOUT
  N4: IC1.no_name_yet#4, R1.pin_1, R2.Pin_1
  N5: IC1.no_name_yet#5, T1.Vout
  N6: IC1.no_name_yet#6, R3.Pin_0, R4.Pin_0
  GND: IC1.no_name_yet#9, IC1.no_name_yet#14, Raspberry_Pi_1.GND, Part1.GND, R2.Pin_0, T1.GND
  N7: IC1.no_name_yet#10, Raspberry_Pi_1.GIPO8
  N8: IC1.no_name_yet#11, Raspberry_Pi_1.GIPO10
  N9: IC1.no_name_yet#12, Raspberry_Pi_1.GIPO9
  N10: IC1.no_name_yet#13, Raspberry_Pi_1.GIPO11
  3V3: IC1.no_name_yet#15, IC1.no_name_yet#16, Raspberry_Pi_1.3v3, Part1.VCC, R1.pin_0, T1.+Vs
  N11: D1.A, R3.Pin_1
  N12: D1.C, R4.Pin_1
